# Fritzing sketch portland_synth (saved by Fritzing 0.9.3b)
breadboards: 2

parts:
  MCU1 = Raspberry Pi Zero
  ADC1 = MCP3008 [package=dil16]
  R3 = Trimmer Potentiometer [maximum_resistance=10kΩ package=THT]
  R4 = Trimmer Potentiometer [maximum_resistance=10kΩ package=THT]
  R5 = Trimmer Potentiometer [maximum_resistance=10kΩ package=THT]
  R6 = Trimmer Potentiometer [maximum_resistance=10kΩ package=THT]
  R7 = Trimmer Potentiometer [maximum_resistance=10kΩ package=THT]
  R8 = Trimmer Potentiometer [maximum_resistance=10kΩ package=THT]
  R9 = Trimmer Potentiometer [maximum_resistance=10kΩ package=THT]
  R10 = Trimmer Potentiometer [maximum_resistance=10kΩ package=THT]
  SW1 = ENCODER_RGB_CA [package=encoder_led_3]
  SW2 = ENCODER_RGB_CA [package=encoder_led_3]

nets:
  N1: MCU1.pin_1, MCU1.pin_17, ADC1.VREF, ADC1.VDD, R3.leg1, R4.leg1, R5.leg1, R6.leg1, R7.leg1, R8.leg1, R9.leg1, R10.leg1, SW1.C, SW2.C
  N2: MCU1.pin_6, MCU1.pin_25, MCU1.pin_34, MCU1.pin_39, ADC1.DGND, ADC1.AGND, R3.leg2, R4.leg2, R5.leg2, R6.leg2, R7.leg2, R8.leg2, R9.leg2, R10.leg2, SW1.B, SW2.B
  N3: MCU1.pin_11, SW2.A
  N4: MCU1.pin_12, SW2.+
  N5: MCU1.pin_13, SW2.-B
  N6: MCU1.pin_19, ADC1.Din
  N7: MCU1.pin_21, ADC1.Dout
  N8: MCU1.pin_23, ADC1.CLK
  N9: MCU1.pin_24, ADC1.CS/SHDN
  N10: MCU1.pin_29, SW1.A
  N11: MCU1.pin_31, SW1.+
  N12: MCU1.pin_33, SW1.-B
  N13: ADC1.CH0, R4.wiper
  N14: ADC1.CH1, R5.wiper
  N15: ADC1.CH2, R6.wiper
  N16: ADC1.CH3, R7.wiper
  N17: ADC1.CH4, R3.wiper
  N18: ADC1.CH5, R8.wiper
  N19: ADC1.CH6, R9.wiper
  N20: ADC1.CH7, R10.wiper
